# Fritzing sketch Counter (saved by Fritzing 0.9.2b)
breadboards: 1

parts:
  IC1 = IC, DIP package, 14 pins [chip_label=74LS74A]
  IC2 = IC, DIP package, 14 pins [chip_label=74LS74A]
  Power_plug1 = Power plug
  LED1 = LED - 5mm [color="Red (633nm)" package="5 mm [THT]"]
  LED2 = LED - 5mm [color="Red (633nm)" package="5 mm [THT]"]
  LED3 = LED - 5mm [color="Red (633nm)" package="5 mm [THT]"]
  LED4 = LED - 5mm [color="Red (633nm)" package="5 mm [THT]"]
  R1 = Resistor [tolerance=±5% resistance=220 package=THT]
  R2 = Resistor [tolerance=±5% resistance=220 package=THT]
  R3 = Resistor [tolerance=±5% resistance=220 package=THT]
  R4 = Resistor [tolerance=±5% resistance=220 package=THT]

nets:
  N1: IC1.pin1, IC1.pin4, IC1.pin10, IC1.pin13, IC1.pin14, IC2.pin1, IC2.pin4, IC2.pin10, IC2.pin13, IC2.pin14, Power_plug1.VCC
  N2: IC1.pin2, IC1.pin6, IC1.pin11
  N3: IC1.pin3, IC2.pin8, IC2.pin12
  N4: IC1.pin5, LED3.anode
  N5: IC1.pin7, IC2.pin7, Power_plug1.GND, R1.Pin_1, R2.Pin_1, R3.Pin_1, R4.Pin_1
  N6: IC1.pin8, IC1.pin12
  N7: IC1.pin9, LED4.anode
  N8: IC2.pin2, IC2.pin6, IC2.pin11
  N9: IC2.pin5, LED1.anode
  N10: IC2.pin9, LED2.anode
  N11: LED1.cathode, R1.Pin_0
  N12: LED2.cathode, R2.Pin_0
  N13: LED3.cathode, R3.Pin_0
  N14: LED4.cathode, R4.Pin_0
